// Logisim project AND.circ as structural Verilog: 1 circuit, main circuit main
module main (
  input  A1,
  input  B1,
  input  A2,
  input  A0,
  input  A1_2,
  input  B2,
  input  A2_2,
  input  A3,
  input  A3_2,
  input  B3,
  input  A4,
  input  A4_2,
  input  A5,
  input  B4,
  input  A6,
  input  A5_2,
  input  A7,
  input  B0,
  input  B5,
  input  B1_2,
  input  A6_2,
  input  B2_2,
  input  B6,
  input  B3_2,
  input  A7_2,
  input  B4_2,
  input  B5_2,
  input  B7,
  input  B6_2,
  input  A8,
  input  B7_2,
  input  B8,
  output S1,
  output S2,
  output S3,
  output S4,
  output OR,
  output S5,
  output S6,
  output S7,
  output S8
);

  and and_1 (S1, A1, B1);
  and and_2 (S2, A2, B2);
  and and_3 (S3, A3, B3);
  and and_4 (S4, A4_2, B4);
  and and_5 (S5, A5_2, B5);
  and and_6 (S6, A6_2, B6);
  and and_7 (S7, A7_2, B7);
  and and_8 (S8, A8, B8);
  and and_9 (OR, A0, A1_2, A2_2, A3_2, A4, A5, A6, A7, B0, B1_2, B2_2, B3_2, B4_2, B5_2, B6_2, B7_2);
endmodule
