// Logisim project OR.circ as structural Verilog: 1 circuit, main circuit main
module main (
  input  a0,
  input  a0_2,
  input  b0,
  input  a1,
  input  a1_2,
  input  a2,
  input  a3,
  input  b1,
  input  a4,
  input  a2_2,
  input  a5,
  input  b2,
  input  a6,
  input  a7,
  input  a3_2,
  input  b0_2,
  input  b3,
  input  b1_2,
  input  a4_2,
  input  b2_2,
  input  b3_2,
  input  b4,
  input  b4_2,
  input  a5_2,
  input  b5,
  input  b5_2,
  input  b6,
  input  b7,
  input  a6_2,
  input  b6_2,
  input  a7_2,
  input  b7_2,
  output S1,
  output S2,
  output S3,
  output OR,
  output S4,
  output S5,
  output S6,
  output S7,
  output S8
);

  or or_1 (S1, a0, b0);
  or or_2 (S2, a1_2, b1);
  or or_3 (S3, a2_2, b2);
  or or_4 (S4, a3_2, b3);
  or or_5 (S5, a4_2, b4);
  or or_6 (S6, a5_2, b5_2);
  or or_7 (S7, a6_2, b6_2);
  or or_8 (S8, a7_2, b7_2);
  or or_9 (OR, a0_2, a1, a2, a3, a4, a5, a6, a7, b0_2, b1_2, b2_2, b3_2, b4_2, b5, b6, b7);
endmodule
