// Logisim project Ula.circ as structural Verilog: 1 circuit, main circuit Somador
module Somador (
  input  Select__1,
  input  Select___0,
  input  Bit_Invert,
  input  Clear,
  input  Clear_2,
  output s3,
  output s2,
  output s1,
  output s0,
  output s3_2,
  output s2_2,
  output s1_2,
  output s0_2
);

  wire adder_1_cout, adder_1_out, and_1_out, and_2_out, and_3_out, and_4_out, and_5_out, and_6_out,
       and_7_out, and_8_out, and_9_out, Clock__tap_8_times_out, Clock__tap_16_times_out, d_ff_1_q, d_ff_2_q,
       d_ff_3_q, d_ff_4_q, d_ff_5_q, d_ff_6_q, d_ff_7_q, d_ff_8_q, d_ff_9_q, d_ff_10_q, d_ff_11_q, d_ff_12_q,
       d_ff_13_q, d_ff_14_q, d_ff_15_q, d_ff_16_q, d_ff_17_q, d_ff_18_q, d_ff_19_q, d_ff_20_q, d_ff_21_q,
       d_ff_22_q, d_ff_23_q, d_ff_24_q, d_ff_25_q, d_ff_26_q, d_ff_27_q, d_ff_28_q, d_ff_29_q, d_ff_30_q,
       d_ff_31_q, d_ff_32_q, d_ff_33_q, d_ff_34_q, not_1_out, not_2_out, not_3_out, not_4_out, or_1_out,
       or_2_out, or_3_out, or_4_out, xor_1_out, xor_2_out;

  Clock Clock__tap_16_times (.out(Clock__tap_16_times_out));
  Clock Clock__tap_8_times (.out(Clock__tap_8_times_out));
  D_Flip_Flop d_ff_1 (.clk(Clock__tap_16_times_out), .Q(d_ff_1_q), .reset(Clear));  // open: D, Qn, preset, en
  D_Flip_Flop d_ff_2 (.clk(Clock__tap_16_times_out), .Q(d_ff_2_q), .reset(Clear));  // open: D, Qn, preset, en
  D_Flip_Flop d_ff_3 (.clk(Clock__tap_8_times_out), .Q(d_ff_3_q), .reset(Clear_2));  // open: D, Qn, preset, en
  D_Flip_Flop d_ff_4 (.clk(Clock__tap_8_times_out), .Q(d_ff_4_q), .reset(Clear_2));  // open: D, Qn, preset, en
  D_Flip_Flop d_ff_5 (
    .clk(Clock__tap_16_times_out), .D(d_ff_1_q), .Q(d_ff_5_q), .reset(Clear));  // open: Qn, preset, en
  D_Flip_Flop d_ff_6 (
    .clk(Clock__tap_16_times_out), .D(d_ff_2_q), .Q(d_ff_6_q), .reset(Clear));  // open: Qn, preset, en
  D_Flip_Flop d_ff_7 (
    .clk(Clock__tap_8_times_out), .D(d_ff_3_q), .Q(d_ff_7_q), .reset(Clear_2));  // open: Qn, preset, en
  D_Flip_Flop d_ff_8 (
    .clk(Clock__tap_8_times_out), .D(d_ff_4_q), .Q(d_ff_8_q), .reset(Clear_2));  // open: Qn, preset, en
  D_Flip_Flop d_ff_9 (
    .clk(Clock__tap_16_times_out), .D(d_ff_5_q), .Q(d_ff_9_q), .reset(Clear));  // open: Qn, preset, en
  D_Flip_Flop d_ff_10 (
    .clk(Clock__tap_16_times_out), .D(d_ff_6_q), .Q(d_ff_10_q), .reset(Clear));  // open: Qn, preset, en
  D_Flip_Flop d_ff_11 (
    .clk(Clock__tap_8_times_out), .D(d_ff_7_q), .Q(d_ff_11_q), .reset(Clear_2));  // open: Qn, preset, en
  D_Flip_Flop d_ff_12 (
    .clk(Clock__tap_8_times_out), .D(d_ff_8_q), .Q(d_ff_12_q), .reset(Clear_2));  // open: Qn, preset, en
  D_Flip_Flop d_ff_13 (
    .clk(Clock__tap_16_times_out), .D(d_ff_9_q), .Q(d_ff_13_q), .reset(Clear));  // open: Qn, preset, en
  D_Flip_Flop d_ff_14 (
    .clk(Clock__tap_16_times_out), .D(d_ff_10_q), .Q(d_ff_14_q), .reset(Clear));  // open: Qn, preset, en
  D_Flip_Flop d_ff_15 (
    .clk(Clock__tap_8_times_out), .D(d_ff_11_q), .Q(d_ff_15_q), .reset(Clear_2));  // open: Qn, preset, en
  D_Flip_Flop d_ff_16 (
    .clk(Clock__tap_8_times_out), .D(d_ff_12_q), .Q(d_ff_16_q), .reset(Clear_2));  // open: Qn, preset, en
  D_Flip_Flop d_ff_17 (
    .clk(Clock__tap_16_times_out), .D(d_ff_13_q), .Q(d_ff_17_q), .reset(Clear));  // open: Qn, preset, en
  D_Flip_Flop d_ff_18 (
    .clk(Clock__tap_16_times_out), .D(d_ff_14_q), .Q(d_ff_18_q), .reset(Clear));  // open: Qn, preset, en
  D_Flip_Flop d_ff_19 (
    .clk(Clock__tap_8_times_out), .D(d_ff_15_q), .Q(d_ff_19_q), .reset(Clear_2));  // open: Qn, preset, en
  D_Flip_Flop d_ff_20 (
    .clk(Clock__tap_8_times_out), .D(d_ff_16_q), .Q(d_ff_20_q), .reset(Clear_2));  // open: Qn, preset, en
  D_Flip_Flop d_ff_21 (
    .clk(Clock__tap_16_times_out), .D(d_ff_17_q), .Q(d_ff_21_q), .reset(Clear));  // open: Qn, preset, en
  D_Flip_Flop d_ff_22 (
    .clk(Clock__tap_16_times_out), .D(d_ff_18_q), .Q(d_ff_22_q), .reset(Clear));  // open: Qn, preset, en
  D_Flip_Flop d_ff_23 (
    .clk(Clock__tap_8_times_out), .D(d_ff_19_q), .Q(d_ff_23_q), .reset(Clear_2));  // open: Qn, preset, en
  D_Flip_Flop d_ff_24 (
    .clk(Clock__tap_8_times_out), .D(d_ff_20_q), .Q(d_ff_24_q), .reset(Clear_2));  // open: Qn, preset, en
  D_Flip_Flop d_ff_25 (
    .clk(Clock__tap_16_times_out), .D(d_ff_21_q), .Q(d_ff_25_q), .reset(Clear));  // open: Qn, preset, en
  D_Flip_Flop d_ff_26 (
    .clk(Clock__tap_16_times_out), .D(d_ff_22_q), .Q(d_ff_26_q), .reset(Clear));  // open: Qn, preset, en
  D_Flip_Flop d_ff_27 (
    .clk(Clock__tap_8_times_out), .D(d_ff_23_q), .Q(d_ff_27_q), .reset(Clear_2));  // open: Qn, preset, en
  D_Flip_Flop d_ff_28 (
    .clk(Clock__tap_8_times_out), .D(d_ff_24_q), .Q(d_ff_28_q), .reset(Clear_2));  // open: Qn, preset, en
  D_Flip_Flop d_ff_29 (
    .clk(Clock__tap_16_times_out), .D(d_ff_25_q), .Q(d_ff_29_q), .reset(Clear));  // open: Qn, preset, en
  D_Flip_Flop d_ff_30 (
    .clk(Clock__tap_16_times_out), .D(d_ff_26_q), .Q(d_ff_30_q), .reset(Clear));  // open: Qn, preset, en
  D_Flip_Flop d_ff_31 (
    .clk(Clock__tap_8_times_out), .D(d_ff_27_q), .Q(d_ff_31_q), .reset(Clear_2));  // open: Qn, preset, en
  D_Flip_Flop d_ff_32 (
    .clk(Clock__tap_8_times_out), .D(d_ff_28_q), .Q(d_ff_32_q), .reset(Clear_2));  // open: Qn, preset, en
  Adder #(.width(1)) adder_1 (.a(d_ff_31_q), .b(d_ff_32_q), .out(adder_1_out), .cin(d_ff_33_q), .cout(adder_1_cout));
  D_Flip_Flop d_ff_33 (
    .clk(Clock__tap_8_times_out), .D(adder_1_cout), .Q(d_ff_33_q), .reset(Clear_2));  // open: Qn, preset, en
  D_Flip_Flop d_ff_34 (
    .clk(Clock__tap_16_times_out), .D(or_3_out), .Q(d_ff_34_q), .reset(Clear));  // open: Qn, preset, en
  D_Flip_Flop d_ff_35 (.clk(Clock__tap_8_times_out), .D(adder_1_out), .Q(s3), .reset(Clear_2));  // open: Qn, preset, en
  D_Flip_Flop d_ff_36 (.clk(Clock__tap_8_times_out), .D(s3), .Q(s2), .reset(Clear_2));  // open: Qn, preset, en
  not not_1 (not_1_out, d_ff_30_q);
  D_Flip_Flop d_ff_37 (.clk(Clock__tap_8_times_out), .D(s2), .Q(s1), .reset(Clear_2));  // open: Qn, preset, en
  not not_2 (not_2_out, Bit_Invert);
  D_Flip_Flop d_ff_38 (.clk(Clock__tap_8_times_out), .D(s1), .Q(s0), .reset(Clear_2));  // open: Qn, preset, en
  and and_1 (and_1_out, d_ff_30_q, Bit_Invert);
  and and_2 (and_2_out, not_2_out, not_1_out);
  or or_1 (or_1_out, and_1_out, and_2_out);
  D_Flip_Flop d_ff_39 (.clk(Clock__tap_8_times_out), .D(s0), .Q(s3_2), .reset(Clear_2));  // open: Qn, preset, en
  and and_3 (and_3_out, d_ff_29_q, or_1_out);
  or or_2 (or_2_out, d_ff_29_q, or_1_out);
  D_Flip_Flop d_ff_40 (.clk(Clock__tap_8_times_out), .D(s3_2), .Q(s2_2), .reset(Clear_2));  // open: Qn, preset, en
  and and_4 (and_4_out, d_ff_29_q, or_1_out);
  D_Flip_Flop d_ff_41 (.clk(Clock__tap_8_times_out), .D(s2_2), .Q(s1_2), .reset(Clear_2));  // open: Qn, preset, en
  xor xor_1 (xor_1_out, d_ff_29_q, or_1_out);
  xor xor_2 (xor_2_out, xor_1_out, d_ff_34_q);
  and and_5 (and_5_out, d_ff_34_q, xor_1_out);
  or or_3 (or_3_out, and_5_out, and_4_out);
  D_Flip_Flop d_ff_42 (.clk(Clock__tap_8_times_out), .D(s1_2), .Q(s0_2), .reset(Clear_2));  // open: Qn, preset, en
  not not_3 (not_3_out, Select__1);
  not not_4 (not_4_out, Select___0);
  and and_6 (and_6_out, and_3_out, not_3_out, not_4_out);
  and and_7 (and_7_out, or_2_out, Select___0, not_3_out);
  and and_8 (and_8_out, xor_2_out, Select__1, not_4_out);
  and and_9 (and_9_out, Select__1, Select___0);
  or or_4 (or_4_out, and_6_out, and_7_out, and_8_out, and_9_out);
  LED led_1 (.in(or_4_out));

  // Notes on the sheet:
  //   A
  //   B
  //   A
  //   B
  //   A
  //   B
endmodule
