// Logisim project somador_serial_8bit.circ as structural Verilog: 1 circuit, main circuit main
module main (
  input  A0,
  input  B0,
  input  CarryIn___para_o_somador_puro__deve_ficar_setado_em_0,
  input  B_Invert,
  input  A1,
  input  B1,
  input  A2,
  input  B2,
  input  A3,
  input  B3,
  input  A4,
  input  B4,
  input  A5,
  input  B5,
  input  A6,
  input  B6,
  input  A7,
  input  B7,
  output S0___bit_menos_significativo,
  output S1,
  output S2,
  output S3,
  output S4,
  output S5,
  output S6,
  output S7,
  output CarryOut
);

  wire and_1_out, and_2_out, and_3_out, and_4_out, and_5_out, and_6_out, and_7_out, and_8_out, and_9_out,
       and_10_out, and_11_out, and_12_out, and_13_out, and_14_out, and_15_out, and_16_out, or_1_out,
       or_2_out, or_3_out, or_4_out, or_5_out, or_6_out, or_7_out, xor_1_out, xor_2_out, xor_3_out,
       xor_4_out, xor_5_out, xor_6_out, xor_7_out, xor_8_out, xor_9_out, xor_10_out, xor_11_out, xor_12_out,
       xor_13_out, xor_14_out, xor_15_out, xor_16_out;

  xor xor_1 (xor_1_out, B0, B_Invert);
  xor xor_2 (xor_2_out, B1, B_Invert);
  xor xor_3 (xor_3_out, B2, B_Invert);
  xor xor_4 (xor_4_out, B3, B_Invert);
  xor xor_5 (xor_5_out, B4, B_Invert);
  xor xor_6 (xor_6_out, B5, B_Invert);
  xor xor_7 (xor_7_out, B6, B_Invert);
  xor xor_8 (xor_8_out, B7, B_Invert);
  xor xor_9 (xor_9_out, A0, xor_1_out);
  xor xor_10 (xor_10_out, A1, xor_2_out);
  xor xor_11 (xor_11_out, A2, xor_3_out);
  xor xor_12 (xor_12_out, A3, xor_4_out);
  xor xor_13 (xor_13_out, A4, xor_5_out);
  xor xor_14 (xor_14_out, A5, xor_6_out);
  xor xor_15 (xor_15_out, A6, xor_7_out);
  xor xor_16 (xor_16_out, A7, xor_8_out);
  and and_1 (and_1_out, CarryIn___para_o_somador_puro__deve_ficar_setado_em_0, xor_9_out);
  and and_2 (and_2_out, A0, xor_1_out);
  and and_3 (and_3_out, or_1_out, xor_10_out);
  and and_4 (and_4_out, A1, xor_2_out);
  and and_5 (and_5_out, or_2_out, xor_11_out);
  and and_6 (and_6_out, A2, xor_3_out);
  and and_7 (and_7_out, or_3_out, xor_12_out);
  and and_8 (and_8_out, A3, xor_4_out);
  xor xor_17 (S0___bit_menos_significativo, xor_9_out, CarryIn___para_o_somador_puro__deve_ficar_setado_em_0);
  xor xor_18 (S1, xor_10_out, or_1_out);
  xor xor_19 (S2, xor_11_out, or_2_out);
  xor xor_20 (S3, xor_12_out, or_3_out);
  xor xor_21 (S4, xor_13_out, or_4_out);
  and and_9 (and_9_out, or_4_out, xor_13_out);
  and and_10 (and_10_out, A4, xor_5_out);
  xor xor_22 (S5, xor_14_out, or_5_out);
  and and_11 (and_11_out, or_5_out, xor_14_out);
  and and_12 (and_12_out, A5, xor_6_out);
  xor xor_23 (S6, xor_15_out, or_6_out);
  and and_13 (and_13_out, or_6_out, xor_15_out);
  and and_14 (and_14_out, A6, xor_7_out);
  xor xor_24 (S7, xor_16_out, or_7_out);
  and and_15 (and_15_out, or_7_out, xor_16_out);
  and and_16 (and_16_out, A7, xor_8_out);
  or or_1 (or_1_out, and_1_out, and_2_out);
  or or_2 (or_2_out, and_3_out, and_4_out);
  or or_3 (or_3_out, and_5_out, and_6_out);
  or or_4 (or_4_out, and_7_out, and_8_out);
  or or_5 (or_5_out, and_9_out, and_10_out);
  or or_6 (or_6_out, and_11_out, and_12_out);
  or or_7 (or_7_out, and_13_out, and_14_out);
  or or_8 (CarryOut, and_15_out, and_16_out);

  // Notes on the sheet:
  //   para subtrair, Carry In e B invert tem que estar em 1
endmodule
